// Digital circuit 2x16bit_mux.dig as structural Verilog
module _2x16bit_mux (
  input  SEL,
  input  [15:0] B,
  input  [15:0] A,
  output [15:0] OUT
);

  _2x8bit_mux _2x8bit_mux_1 (.SEL(SEL), .B(B[7:0]), .A(A[7:0]), .OUT(OUT[7:0]));
  _2x8bit_mux _2x8bit_mux_2 (.SEL(SEL), .B(B[15:8]), .A(A[15:8]), .OUT(OUT[15:8]));
endmodule
