// Digital circuit 4x8bit_mux.dig as structural Verilog
module _4x8bit_mux (
  input  [1:0] SEL,
  input  [7:0] IN0,
  input  [7:0] IN1,
  input  [7:0] IN2,
  input  [7:0] IN3,
  output [7:0] OUT
);

  wire [3:0] _4x8bit_interleave_1_out0, _4x8bit_interleave_1_out1, _4x8bit_interleave_1_out2,
       _4x8bit_interleave_1_out3, _4x8bit_interleave_1_out4, _4x8bit_interleave_1_out5,
       _4x8bit_interleave_1_out6, _4x8bit_interleave_1_out7;

  _4x8bit_interleave _4x8bit_interleave_1 (
    .WORD0(IN0), .WORD1(IN1), .WORD2(IN2), .WORD3(IN3), .OUT0(_4x8bit_interleave_1_out0),
    .OUT1(_4x8bit_interleave_1_out1), .OUT2(_4x8bit_interleave_1_out2), .OUT3(_4x8bit_interleave_1_out3),
    .OUT4(_4x8bit_interleave_1_out4), .OUT5(_4x8bit_interleave_1_out5), .OUT6(_4x8bit_interleave_1_out6),
    .OUT7(_4x8bit_interleave_1_out7));
  _4x8bit_masked_or _4x8bit_masked_or_1 (
    .SELECT(SEL), .DATA0(_4x8bit_interleave_1_out0), .DATA1(_4x8bit_interleave_1_out1),
    .DATA2(_4x8bit_interleave_1_out2), .DATA3(_4x8bit_interleave_1_out3), .DATA4(_4x8bit_interleave_1_out4),
    .DATA5(_4x8bit_interleave_1_out5), .DATA6(_4x8bit_interleave_1_out6), .DATA7(_4x8bit_interleave_1_out7),
    .OUT0(OUT[0]), .OUT1(OUT[1]), .OUT2(OUT[2]), .OUT3(OUT[3]), .OUT4(OUT[4]), .OUT5(OUT[5]), .OUT6(OUT[6]),
    .OUT7(OUT[7]));
endmodule
