// Digital circuit 8bit_alu.dig as structural Verilog
module _8bit_alu (
  input  CLK,
  input  WFLAGEN,
  input  CLR,
  input  [3:0] OP,
  input  [7:0] A,
  input  [7:0] B,
  output [2:0] FLAGS,
  output [7:0] RESULT
);

  wire or_1_out;
  wire [2:0] nand_1_out;
  wire [7:0] _2x8bit_mux_1_out, _8bit_add_sub_1_result, _8bit_or_nor_xor_and_1_out, _8bit_shifter_1_out;

  _3bit_register_async_clear _3bit_register_async_clear_1 (
    .CLK(CLK), .WEN(WFLAGEN), .WRITE(nand_1_out), .CLR(CLR), .READ(FLAGS));
  _8bit_add_sub _8bit_add_sub_1 (
    .A(A), .B(B), .ADD_SUB(OP[1]), .ADC_SBC(OP[0]), .CIN(FLAGS[0]), .RESULT(_8bit_add_sub_1_result),
    .COUT(nand_1_out[0]));  // open: OVF
  _8bit_or_nor_xor_and _8bit_or_nor_xor_and_1 (
    .SEL(OP[1:0]), .A(A), .B(B), .OUT(_8bit_or_nor_xor_and_1_out), .EQUAL(nand_1_out[1]));
  _8bit_shifter _8bit_shifter_1 (.A(A), .B(B[2:0]), .DIR(OP[0]), .OUT(_8bit_shifter_1_out));
  _2x8bit_mux _2x8bit_mux_1 (
    .SEL(OP[2]), .B(_8bit_or_nor_xor_and_1_out), .A(_8bit_add_sub_1_result), .OUT(_2x8bit_mux_1_out));
  _2x8bit_mux _2x8bit_mux_2 (.SEL(OP[3]), .B(_8bit_shifter_1_out), .A(_2x8bit_mux_1_out), .OUT(RESULT));
  or or_1 (or_1_out, RESULT[0], RESULT[1], RESULT[2], RESULT[3], RESULT[4], RESULT[5], RESULT[6], RESULT[7]);
  nand nand_1 (nand_1_out[2], or_1_out, or_1_out);

  // Notes on the sheet:
  //   Schottky Diode OR
  //   CARRY/BORROW
  //   EQUAL
  //   ZERO
endmodule
