// Digital circuit 8bit_or_nor_xor_and.dig as structural Verilog
module _8bit_or_nor_xor_and (
  input  [1:0] SEL,
  input  [7:0] A,
  input  [7:0] B,
  output [7:0] RESULT
);

  wire [3:0] _1bit_or_nor_xor_and_1_result, _1bit_or_nor_xor_and_2_result, _1bit_or_nor_xor_and_3_result,
       _1bit_or_nor_xor_and_4_result, _1bit_or_nor_xor_and_5_result, _1bit_or_nor_xor_and_6_result,
       _1bit_or_nor_xor_and_7_result, _1bit_or_nor_xor_and_8_result, select2_1_o3;

  select2 select2_1 (
    .S0(SEL[0]), .S1(SEL[1]), .O0(select2_1_o3[0]), .O1(select2_1_o3[1]), .O2(select2_1_o3[2]),
    .O3(select2_1_o3[3]));
  _1bit_or_nor_xor_and _1bit_or_nor_xor_and_1 (.A(A[0]), .B(B[0]), .RESULT(_1bit_or_nor_xor_and_1_result));
  _1bit_or_nor_xor_and _1bit_or_nor_xor_and_2 (.A(A[1]), .B(B[1]), .RESULT(_1bit_or_nor_xor_and_2_result));
  _1bit_or_nor_xor_and _1bit_or_nor_xor_and_3 (.A(A[2]), .B(B[2]), .RESULT(_1bit_or_nor_xor_and_3_result));
  _1bit_or_nor_xor_and _1bit_or_nor_xor_and_4 (.A(A[3]), .B(B[3]), .RESULT(_1bit_or_nor_xor_and_4_result));
  _1bit_or_nor_xor_and _1bit_or_nor_xor_and_5 (.A(A[4]), .B(B[4]), .RESULT(_1bit_or_nor_xor_and_5_result));
  _1bit_or_nor_xor_and _1bit_or_nor_xor_and_6 (.A(A[5]), .B(B[5]), .RESULT(_1bit_or_nor_xor_and_6_result));
  _1bit_or_nor_xor_and _1bit_or_nor_xor_and_7 (.A(A[6]), .B(B[6]), .RESULT(_1bit_or_nor_xor_and_7_result));
  _1bit_or_nor_xor_and _1bit_or_nor_xor_and_8 (.A(A[7]), .B(B[7]), .RESULT(_1bit_or_nor_xor_and_8_result));
  deselect2 deselect2_1 (.BI(_1bit_or_nor_xor_and_1_result), .AI(select2_1_o3), .O(RESULT[0]));
  deselect2 deselect2_2 (.BI(_1bit_or_nor_xor_and_2_result), .AI(select2_1_o3), .O(RESULT[1]));
  deselect2 deselect2_3 (.BI(_1bit_or_nor_xor_and_3_result), .AI(select2_1_o3), .O(RESULT[2]));
  deselect2 deselect2_4 (.BI(_1bit_or_nor_xor_and_4_result), .AI(select2_1_o3), .O(RESULT[3]));
  deselect2 deselect2_5 (.BI(_1bit_or_nor_xor_and_5_result), .AI(select2_1_o3), .O(RESULT[4]));
  deselect2 deselect2_6 (.BI(_1bit_or_nor_xor_and_6_result), .AI(select2_1_o3), .O(RESULT[5]));
  deselect2 deselect2_7 (.BI(_1bit_or_nor_xor_and_7_result), .AI(select2_1_o3), .O(RESULT[6]));
  deselect2 deselect2_8 (.BI(_1bit_or_nor_xor_and_8_result), .AI(select2_1_o3), .O(RESULT[7]));
endmodule
