// Digital circuit condition_checker.dig as structural Verilog
module condition_checker (
  input  [2:0] FLAGS,
  input  [1:0] COND,
  output SKIP
);

  wire nand_1_out, nand_2_out, nand_3_out, nand_4_out, nand_5_out, nand_6_out, select2_1_o0, select2_1_o1,
       select2_1_o2, select2_1_o3;

  select2 select2_1 (
    .S0(COND[1]), .S1(COND[0]), .O0(select2_1_o0), .O1(select2_1_o1), .O2(select2_1_o2), .O3(select2_1_o3));
  nand nand_1 (nand_1_out, FLAGS[0], select2_1_o1);
  nand nand_2 (nand_2_out, FLAGS[1], select2_1_o2);
  nand nand_3 (nand_3_out, FLAGS[2], select2_1_o3);
  nand nand_4 (nand_4_out, nand_1_out, nand_1_out);
  nand nand_5 (nand_5_out, nand_2_out, nand_2_out);
  nand nand_6 (nand_6_out, nand_3_out, nand_3_out);
  or or_1 (SKIP, select2_1_o0, nand_4_out, nand_5_out, nand_6_out);
endmodule
