// Digital circuit cpu.dig as structural Verilog
module cpu (
  input  RESET,
  input  HALT,
  input  CONTINUE,
  input  CLKEN,
  input  STEP,
  input  clk,
  output IOEN,
  output IOREN,
  output IOWEN,
  output [7:0] IODATA,
  output [14:0] IOADDR
);

  wire ASSEL, BSSEL, condition_checker_1_p1, condition_checker_1_p3, Control_clkout, Control_ishalted,
       Control_reset_2, FWEN, nand_1_out, nand_2_out, nand_3_out, nand_5_out, nand_7_out, nand_8_out,
       nand_9_out, nand_10_out, oprom_1_p5, oprom_1_p6, oprom_1_p11, PCSEL, PRWEN, RSSEL, RWEN;
  wire [1:0] program_memory_1_cond, program_memory_1_rd, program_memory_1_ro1, program_memory_1_ro2;
  wire [3:0] program_counter_1_r, program_counter_1_r_2, program_counter_1_r_3, program_counter_1_r_4,
       program_memory_1_aluop, program_memory_1_opcode;
  wire [7:0] _2x8bit_mux_1_out, _4x8bit_register_file_async_clear_1_p7,
       _4x8bit_register_file_async_clear_1_p8, _4x8bit_register_file_async_clear_1_p9, _8bit_alu_1_p8,
       _8bit_register_async_clear_1_read;
  wire [15:0] _2x16bit_mux_1_p1, _2x16bit_mux_1_p2, program_memory_1_imm;

  clock Control (
    .RESET(RESET), .HALT(HALT), .CONTINUE(CONTINUE), .CLKHALT(oprom_1_p11), .CLKIN(clk), .STEP(STEP),
    .CLKEN(CLKEN), .ISHALTED(Control_ishalted), .RESET_2(Control_reset_2), .CLKOUT(Control_clkout));
  LED HALTED (.in(Control_ishalted));
  Seven_Seg_Hex seven_seg_hex_1 (.d(program_counter_1_r_4), .dp(1'b0));
  nand nand_1 (nand_1_out, Control_clkout, Control_clkout);
  Seven_Seg_Hex seven_seg_hex_2 (.d(program_counter_1_r_3), .dp(1'b0));
  Seven_Seg_Hex seven_seg_hex_3 (.d(program_counter_1_r_2), .dp(1'b0));
  Seven_Seg_Hex seven_seg_hex_4 (.d(program_counter_1_r), .dp(1'b0));
  program_memory program_memory_1 (
    .ADR({program_counter_1_r_4, program_counter_1_r_3, program_counter_1_r_2, program_counter_1_r}),
    .OPCODE(program_memory_1_opcode), .COND(program_memory_1_cond), .ALUOP(program_memory_1_aluop),
    .RD(program_memory_1_rd), .RO1(program_memory_1_ro1), .RO2(program_memory_1_ro2),
    .IMM(program_memory_1_imm));
  program_counter program_counter_1 (
    .CLK(Control_clkout), .W(_2x16bit_mux_1_p1), .CLR(Control_reset_2),
    .R({program_counter_1_r_4, program_counter_1_r_3, program_counter_1_r_2, program_counter_1_r}));
  // _2x16bit_mux _2x16bit_mux_1: pin names not known; wires that end beside it: _2x16bit_mux_1_p1, _2x16bit_mux_1_p2, {IOEN, IOADDR}, PCSEL
  _16bit_incrementer _16bit_incrementer_1 (
    .IN({program_counter_1_r_4, program_counter_1_r_3, program_counter_1_r_2, program_counter_1_r}),
    .OUT(_2x16bit_mux_1_p2));
  // _4x8bit_register_file_async_clear _4x8bit_register_file_async_clear_1: pin names not known; wires that end beside it: nand_1_out, Control_reset_2, program_memory_1_rd, program_memory_1_ro1, program_memory_1_ro2, RWEN, _4x8bit_register_file_async_clear_1_p7, _4x8bit_register_file_async_clear_1_p8, _4x8bit_register_file_async_clear_1_p9
  _8bit_register_async_clear _8bit_register_async_clear_1 (
    .CLK(nand_1_out), .WEN(PRWEN), .WRITE(_2x8bit_mux_1_out), .CLR(Control_reset_2),
    .READ(_8bit_register_async_clear_1_read));
  // condition_checker condition_checker_1: pin names not known; wires that end beside it: condition_checker_1_p1, program_memory_1_cond, condition_checker_1_p3
  // _2x16bit_mux _2x16bit_mux_2: pin names not known; wires that end beside it: ASSEL, program_memory_1_imm, {_8bit_register_async_clear_1_read, _4x8bit_register_file_async_clear_1_p8}, {IOEN, IOADDR}
  _2x8bit_mux _2x8bit_mux_1 (
    .SEL(BSSEL), .B(_4x8bit_register_file_async_clear_1_p9), .A(program_memory_1_imm[7:0]),
    .OUT(_2x8bit_mux_1_out));
  _2x8bit_mux _2x8bit_mux_2 (.SEL(RSSEL), .B(IODATA), .A(_8bit_alu_1_p8), .OUT(_4x8bit_register_file_async_clear_1_p7));
  // oprom oprom_1: pin names not known; wires that end beside it: condition_checker_1_p3, program_memory_1_opcode, RWEN, FWEN, oprom_1_p5, oprom_1_p6, BSSEL, ASSEL, RSSEL, PCSEL, oprom_1_p11, PRWEN
  // _8bit_alu _8bit_alu_1: pin names not known; wires that end beside it: nand_1_out, FWEN, Control_reset_2, program_memory_1_aluop, _4x8bit_register_file_async_clear_1_p8, _2x8bit_mux_1_out, condition_checker_1_p1, _8bit_alu_1_p8
  assign IODATA = nand_3_out ? _4x8bit_register_file_async_clear_1_p9 : 8'bz;  // Driver driver_1
  nand nand_2 (nand_2_out, IOEN, IOEN);
  nand nand_3 (nand_3_out, nand_1_out, oprom_1_p5);
  nand nand_4 (IOREN, nand_3_out, nand_3_out);
  nand nand_5 (nand_5_out, nand_1_out, oprom_1_p6);
  nand nand_6 (IOWEN, nand_5_out, nand_5_out);
  nand nand_7 (nand_7_out, IOWEN, nand_2_out);
  nand nand_8 (nand_8_out, IOREN, nand_2_out);
  nand nand_9 (nand_9_out, nand_7_out, nand_7_out);
  nand nand_10 (nand_10_out, nand_8_out, nand_8_out);
  RAMSinglePortSel #(.AddrBits(15), .Bits(8)) ramsingleportsel_1 (
    .A(IOADDR), .CS(1'b1), .WE(nand_9_out), .OE(nand_10_out), .D(IODATA));
  Seven_Seg_Hex seven_seg_hex_5 (.d({1'b0, IOADDR[14:12]}), .dp(1'b0));
  Seven_Seg_Hex seven_seg_hex_6 (.d(IOADDR[11:8]), .dp(1'b0));
  Seven_Seg_Hex seven_seg_hex_7 (.d(IOADDR[7:4]), .dp(1'b0));
  Seven_Seg_Hex seven_seg_hex_8 (.d(IOADDR[3:0]), .dp(1'b0));
  Seven_Seg_Hex seven_seg_hex_9 (.d(IODATA[7:4]), .dp(1'b0));
  Seven_Seg_Hex seven_seg_hex_10 (.d(IODATA[3:0]), .dp(1'b0));

  // Notes on the sheet:
  //   clk: Hz: 100
  //   CONTROL
  //   INSTRUCTION
  //   DECODE
  //   IO
endmodule
