// Digital circuit oprom.dig as structural Verilog
module oprom (
  input  SKIP,
  input  [3:0] OPCODE,
  output RWEN,
  output FWEN,
  output IOREN,
  output IOWEN,
  output BSSEL,
  output ASSEL,
  output RSSEL,
  output PCSSEL,
  output HALT,
  output PRWEN
);

  wire nand_1_out, nand_2_out, nand_3_out, nand_4_out, nand_9_out, nand_10_out, nand_11_out, nand_12_out,
       nand_13_out;
  wire [3:0] nand_5_out;

  nand nand_1 (nand_1_out, SKIP, OPCODE[0]);
  nand nand_2 (nand_2_out, SKIP, OPCODE[1]);
  nand nand_3 (nand_3_out, SKIP, OPCODE[2]);
  nand nand_4 (nand_4_out, SKIP, OPCODE[3]);
  nand nand_5 (nand_5_out[0], nand_1_out, nand_1_out);
  nand nand_6 (nand_5_out[1], nand_2_out, nand_2_out);
  nand nand_7 (nand_5_out[2], nand_3_out, nand_3_out);
  nand nand_8 (nand_5_out[3], nand_4_out, nand_4_out);
  nand nand_9 (nand_9_out, nand_5_out[3], nand_5_out[2]);
  nand nand_10 (nand_10_out, nand_5_out[1], nand_5_out[0]);
  nand nand_11 (nand_11_out, nand_9_out, nand_9_out);
  nand nand_12 (nand_12_out, nand_10_out, nand_10_out);
  ROM #(.AddrBits(4), .Bits(9)) rom_1 (
    .A(nand_5_out), .sel(1'b1), .D({PRWEN, PCSSEL, RSSEL, ASSEL, BSSEL, IOWEN, IOREN, FWEN, RWEN}));
  nand nand_13 (nand_13_out, nand_11_out, nand_12_out);
  nand nand_14 (HALT, nand_13_out, nand_13_out);

  // Notes on the sheet:
  //   rom_1 loads microcode.bin
endmodule
