// Digital circuit cpu.dig as structural Verilog
module cpu (
  input  RESET,
  input  HALT,
  input  CONTINUE,
  input  CLKEN,
  input  STEP,
  input  clk
);

  wire _2x16bit_mux_1_p3, _2x16bit_mux_1_p4, CLK_t, CLK_t_t, Control_ishalted, Control_reset_2, nand_3_out,
       nand_4_out, nand_5_out, nand_6_out, nand_7_out, nand_8_out, nand_9_out, nand_10_out, nand_11_out,
       oprom_1_adrwen, oprom_1_halt, oprom_1_ioren, oprom_1_iowen, oprom_1_pcssel, oprom_1_regwen, or_1_out,
       program_memory_1_opsel, program_memory_1_writeflag;
  wire [2:0] program_memory_1_rd, program_memory_1_ro1, program_memory_1_ro2;
  wire [3:0] _8bit_alu_1_p6, program_counter_1_r, program_counter_1_r_2, program_counter_1_r_3,
       program_counter_1_r_4, program_memory_1_opcode;
  wire [7:0] _2x8bit_mux_1_out, _2x8bit_mux_2_out, _8bit_alu_1_p5, driver_1_out, register_bank_1_read_0,
       register_bank_1_read_1, register_bank_1_read_flag;
  wire [15:0] _2x16bit_mux_1_p1, _2x16bit_mux_1_p2, _2x16bit_mux_2_p2, _2x16bit_mux_3_p4,
       program_memory_1_imm;

  Seven_Seg_Hex seven_seg_hex_1 (.d(program_counter_1_r_4), .dp(1'b0));
  clock Control (
    .RESET(RESET), .HALT(HALT), .CONTINUE(CONTINUE), .CLKHALT(oprom_1_halt), .CLKIN(clk), .STEP(STEP),
    .CLKEN(CLKEN), .ISHALTED(Control_ishalted), .RESET_2(Control_reset_2), .CLKOUT(CLK_t));
  Seven_Seg_Hex seven_seg_hex_2 (.d(program_counter_1_r_3), .dp(1'b0));
  Seven_Seg_Hex seven_seg_hex_3 (.d(program_counter_1_r_2), .dp(1'b0));
  Seven_Seg_Hex seven_seg_hex_4 (.d(program_counter_1_r), .dp(1'b0));
  LED HALTED (.in(Control_ishalted));
  nand nand_1 (CLK_t_t, CLK_t, CLK_t);
  program_counter program_counter_1 (
    .CLK(CLK_t_t), .W(_2x16bit_mux_1_p1), .CLR(Control_reset_2),
    .R({program_counter_1_r_4, program_counter_1_r_3, program_counter_1_r_2, program_counter_1_r}));
  // _2x16bit_mux _2x16bit_mux_1: pin names not known; wires that end beside it: _2x16bit_mux_1_p1, _2x16bit_mux_1_p2, _2x16bit_mux_1_p3, _2x16bit_mux_1_p4
  program_memory program_memory_1 (
    .ADR({program_counter_1_r_4, program_counter_1_r_3, program_counter_1_r_2, program_counter_1_r}),
    .OPCODE(program_memory_1_opcode), .OPSEL(program_memory_1_opsel), .RD(program_memory_1_rd),
    .RO1(program_memory_1_ro1), .RO2(program_memory_1_ro2), .IMM(program_memory_1_imm),
    .WRITEFLAG(program_memory_1_writeflag));
  _16bit_incrementer _16bit_incrementer_1 (
    .IN({program_counter_1_r_4, program_counter_1_r_3, program_counter_1_r_2, program_counter_1_r}),
    .OUT(_2x16bit_mux_1_p2));
  oprom oprom_1 (
    .OPCODE(program_memory_1_opcode), .REGWEN(oprom_1_regwen), .ADRWEN(oprom_1_adrwen),
    .IOREN(oprom_1_ioren), .IOWEN(oprom_1_iowen), .PCSSEL(oprom_1_pcssel), .HALT(oprom_1_halt));
  nand nand_2 (_2x16bit_mux_1_p4, nand_3_out, nand_3_out);
  // _2x16bit_mux _2x16bit_mux_2: pin names not known; wires that end beside it: _2x16bit_mux_1_p3, _2x16bit_mux_2_p2, program_memory_1_imm, program_memory_1_opsel
  nand nand_3 (nand_3_out, oprom_1_pcssel, nand_4_out);
  nand nand_4 (nand_4_out, nand_6_out, nand_5_out);
  register_bank register_bank_1 (
    .CLK(CLK_t), .CLR(Control_reset_2), .WSEL(program_memory_1_rd), .RSEL0(program_memory_1_ro1),
    .RSEL1(program_memory_1_ro2), .DATA_GP(_2x8bit_mux_2_out), .DATA_FLAG({4'b0000, _8bit_alu_1_p6}),
    .DATA_ADDR(program_memory_1_imm), .WRITE_GP(oprom_1_regwen), .WRITE_FLAG(program_memory_1_writeflag),
    .WRITE_ADDR(oprom_1_adrwen), .READ_0(register_bank_1_read_0), .READ_1(register_bank_1_read_1),
    .READ_FLAG(register_bank_1_read_flag), .READ_ADDR(_2x16bit_mux_2_p2));
  nand nand_5 (nand_5_out, nand_7_out, nand_8_out);
  nand nand_6 (nand_6_out, program_memory_1_opcode[0], nand_7_out);
  nand nand_7 (nand_7_out, program_memory_1_opcode[0], nand_8_out);
  nand nand_8 (nand_8_out, or_1_out, or_1_out);
  or or_1 (or_1_out, register_bank_1_read_1[0], register_bank_1_read_1[1], register_bank_1_read_1[2], register_bank_1_read_1[3], register_bank_1_read_1[4], register_bank_1_read_1[5], register_bank_1_read_1[6], register_bank_1_read_1[7]);
  _2x8bit_mux _2x8bit_mux_1 (
    .SEL(program_memory_1_opsel), .B(program_memory_1_imm[7:0]), .A(register_bank_1_read_1),
    .OUT(_2x8bit_mux_1_out));
  // _2x16bit_mux _2x16bit_mux_3: pin names not known; wires that end beside it: program_memory_1_opsel, program_memory_1_imm, _2x16bit_mux_2_p2, _2x16bit_mux_3_p4
  // _8bit_alu _8bit_alu_1: pin names not known; wires that end beside it: program_memory_1_opcode, register_bank_1_read_0, _2x8bit_mux_1_out, register_bank_1_read_flag[1], _8bit_alu_1_p5, _8bit_alu_1_p6[0], _8bit_alu_1_p6[1], _8bit_alu_1_p6[2], _8bit_alu_1_p6[3]
  _2x8bit_mux _2x8bit_mux_2 (
    .SEL(program_memory_1_opcode[3]), .B(driver_1_out), .A(_8bit_alu_1_p5), .OUT(_2x8bit_mux_2_out));
  nand nand_9 (nand_9_out, oprom_1_iowen, CLK_t);
  nand nand_10 (nand_10_out, nand_9_out, nand_9_out);
  assign driver_1_out = nand_11_out ? register_bank_1_read_1 : 8'bz;  // Driver driver_1
  RAMSinglePortSel #(.AddrBits(16), .Bits(8)) ramsingleportsel_1 (
    .A(_2x16bit_mux_3_p4), .CS(1'b1), .WE(nand_10_out), .OE(oprom_1_ioren), .D(driver_1_out));
  nand nand_11 (nand_11_out, oprom_1_ioren, oprom_1_ioren);

  // Notes on the sheet:
  //   clk: Hz: 100
  //   Schottky Diode OR
endmodule
