// Digital circuit oprom.dig as structural Verilog
module oprom (
  input  [6:0] OPCODE,
  output REGWEN,
  output IOREN,
  output IOWEN,
  output PCSSEL,
  output HALT,
  output OPSEL,
  output FWEN,
  output ADRSEL,
  output RESSEL,
  output ZINV,
  output [2:0] ALUOP,
  output CRYEN
);

  wire [15:14] rom_1_d;

  ROM #(.AddrBits(7), .Bits(16)) rom_1 (
    .A(OPCODE), .sel(1'b1),
    .D({rom_1_d, CRYEN, ALUOP, ZINV, RESSEL, ADRSEL, FWEN, OPSEL, HALT, PCSSEL, IOWEN, IOREN, REGWEN}));

  // Notes on the sheet:
  //   rom_1 loads microcode.bin
endmodule
